// Logisim project Ext8vers16.circ as structural Verilog: 1 circuit, main circuit main
module main (
  input  [7:0] in_1,
  input  [7:0] in_2,
  output [15:0] out_3,
  output [15:0] out_4
);

  assign out_3 = {{8{in_1[7]}}, in_1};  // Bit_Extender bit_extender_1

  assign out_4 = {{9{in_2[7]}}, in_2[6:0]};
endmodule
