// Logisim project LC3_etu.circ as structural Verilog: 10 circuits, main circuit main
module main (
  input  Reset,
  input  ResetRAM,
  output [2:0] out_3
);

  wire Arith, Branch, Clock, Clock_out, Exec, Fetch, getcst_1_usecst, Load, nzp_1_cond, ramctrl_1_memload,
       ramctrl_1_memstore, Store, WriteReg;
  wire [1:0] GetOp;
  wire [8:0] Offset9;
  wire [15:0] Addr, alu_1_output, getcst_1_cst, IR, MemIN, MemOUT, multiplexer_1_out, PC, R0, R1, R2, R3, R4,
       R5, R6, R7, registres_1_out_sr1, registres_1_out_sr2;

  Clock u_Clock (.out(Clock_out));
  NZP nzp_1 (.NZP(out_3), .WriteReg(WriteReg), .Cond(nzp_1_cond), .IR(multiplexer_1_out), .IN(MemIN), .Clock(Clock));
  Seq seq_1 (.ClockOrig(Clock_out), .reset(Reset), .Fetch(Fetch), .Exec(Exec), .Clock(Clock));
  LED led_1 (.in(Clock_out));
  RegPC regpc_1 (.Offset9(Offset9), .Cond(nzp_1_cond), .Branch(Branch), .Clock(Exec), .Reset(Reset), .PC(PC));
  // Probe on PC
  GetAddr getaddr_1 (.PC(PC), .Addr(Addr), .Offset9(Offset9), .Fetch(Fetch), .Load(Load), .Store(Store));
  // Probe on Addr
  LED led_2 (.in(Fetch));
  LED led_3 (.in(Exec));
  // Probe on MemIN
  RamCtrl ramctrl_1 (
    .Store(Store), .Fetch(Fetch), .Exec(Exec), .Load(Load), .MemStore(ramctrl_1_memstore),
    .MemLoad(ramctrl_1_memload), .Clock(Clock));
  // Probe on PC
  // Probe on IR
  DecodeIR decodeir_1 (
    .Jump(Branch), .WriteReg(WriteReg), .IR(IR), .Load(Load), .Store(Store), .Arith(Arith), .GetOp(GetOp),
    .Offset9(Offset9));
  // Probe on MemOUT
  RAM #(.addrWidth(16), .dataWidth(16), .bus("separate")) ram_1 (
    .addr(Addr), .din(MemIN), .data(MemOUT), .str(ramctrl_1_memstore), .clk(ramctrl_1_memstore),
    .ld(ramctrl_1_memload), .clr(ResetRAM));  // open: sel
  // Probe on R0
  // Probe on R4
  // Probe on IR
  Register #(.width(16), .trigger("falling")) RegIR (.D(MemOUT), .Q(IR), .clk(Fetch), .clr(Reset));  // open: en
  // Probe on R1
  // Probe on R5
  // Probe on R2
  // Probe on R6
  Registres registres_1 (
    .SR1(IR[8:6]), .IN(multiplexer_1_out), .SR2(IR[2:0]), .WriteReg(WriteReg), .DR_SR(IR[11:9]),
    .OUT_SR1(registres_1_out_sr1), .OUT_SR2(registres_1_out_sr2), .OUT_SR(MemIN), .R0(R0), .R1(R1), .R2(R2),
    .R3(R3), .R4(R4), .R5(R5), .R6(R6), .R7(R7), .Reset(Reset), .Clock(Exec));
  // Probe on IR[11:9]
  // Probe on IR[8:6]
  // Probe on IR[2:0]
  // Probe on registres_1_out_sr1
  ALU alu_1 (
    .UseCst(getcst_1_usecst), .e2(GetOp), .Input1(registres_1_out_sr1), .Input2(registres_1_out_sr2),
    .Cst(getcst_1_cst), .Output(alu_1_output));
  // Probe on getcst_1_cst
  GetCst getcst_1 (.IR(IR), .Cst(getcst_1_cst), .UseCst(getcst_1_usecst));
  // Probe on multiplexer_1_out
  // Probe on registres_1_out_sr2
  // Probe on R3
  // Probe on R7
  // Probe on R0
  // Probe on R1
  // Probe on R2
  // Probe on R3
  // Probe on R4
  // Probe on R5
  // Probe on R6
  // Probe on R7
  // Probe on alu_1_output
  Multiplexer #(.width(16)) multiplexer_1 (
    .in0(alu_1_output), .in1(MemOUT), .out(multiplexer_1_out), .sel(Load));  // open: en

  // Notes on the sheet:
  //   RAM
endmodule

module ALU (
  input  [15:0] Input1,
  input  [15:0] Input2,
  input  [15:0] Cst,
  input  UseCst,
  input  [1:0] e2,
  output [15:0] Output
);

  wire [15:0] adder_1_out, and_1_out, multiplexer_1_out, not_1_out;

  Multiplexer #(.width(16), .enable("false")) multiplexer_1 (
    .in0(Input2), .in1(Cst), .out(multiplexer_1_out), .sel(UseCst));
  Adder #(.width(16)) adder_1 (.a(multiplexer_1_out), .b(Input1), .out(adder_1_out));  // open: cin, cout
  assign and_1_out = Input1 & multiplexer_1_out;  // AND_Gate and_1, 16 bits wide
  Multiplexer #(.select(2), .width(16), .enable("false")) multiplexer_2 (
    .in0(adder_1_out), .in1(and_1_out), .in2(not_1_out), .out(Output), .sel(e2));  // open: in3
  assign not_1_out = ~Input1;  // NOT_Gate not_1, 16 bits wide
endmodule

module DecodeIR (
  input  [15:0] IR,
  output Jump,
  output Arith,
  output WriteReg,
  output Load,
  output Store,
  output [1:0] GetOp,
  output [8:0] Offset9
);

  wire not_1_out, not_2_out, not_3_out, not_4_out;

  not not_1 (not_1_out, IR[13]);
  and and_1 (Store, IR[12], IR[13]);
  not not_2 (not_2_out, IR[12]);
  and and_2 (Load, not_2_out, IR[13]);
  not not_3 (not_3_out, IR[13]);
  and and_3 (Jump, not_3_out, not_4_out);
  not not_4 (not_4_out, IR[12]);
  and and_4 (Arith, IR[12], not_1_out);
  xor xor_1 (WriteReg, Arith, Load);

  assign GetOp = IR[15:14];
  assign Offset9 = IR[8:0];
endmodule

module GetAddr (
  input  [8:0] Offset9,
  input  [15:0] PC,
  input  Load,
  input  Store,
  input  Fetch,
  output [15:0] Addr
);

  wire and_1_out, not_1_out, or_1_out;
  wire [8:0] adder_1_out;

  or or_1 (or_1_out, Load, Store);
  not not_1 (not_1_out, Fetch);
  Multiplexer #(.width(16)) multiplexer_1 (
    .in0(PC), .in1({PC[15:9], adder_1_out}), .out(Addr), .sel(and_1_out));  // open: en
  and and_1 (and_1_out, not_1_out, or_1_out);
  Adder #(.width(9)) adder_1 (.a(Offset9), .b(PC[8:0]), .out(adder_1_out), .cin(1'b1));  // open: cout
endmodule

module GetCst (
  input  [15:0] IR,
  output [15:0] Cst,
  output UseCst
);

  assign Cst = {{11{IR[4]}}, IR[4:0]};  // Bit_Extender bit_extender_1

  assign UseCst = IR[5];
endmodule

module NZP (
  input  [15:0] IN,
  input  WriteReg,
  input  Clock,
  input  [15:0] IR,
  output [2:0] NZP,
  output Cond
);

  wire [2:0] and_1_out, comparator_1_gt;

  Comparator #(.width(16)) comparator_1 (
    .a(IN), .b({16{1'b0}}), .gt(comparator_1_gt[0]), .eq(comparator_1_gt[1]), .lt(comparator_1_gt[2]));
  Register #(.width(3), .trigger("falling")) Registre_3_bits (
    .D(comparator_1_gt), .en(WriteReg), .Q(NZP), .clk(Clock));  // open: clr
  assign and_1_out = NZP & IR[11:9];  // AND_Gate and_1, 3 bits wide
  or or_1 (Cond, and_1_out[0], and_1_out[1], and_1_out[2]);

  // Notes on the sheet:
  //   nzp dans IR
  //   test nzp
endmodule

module RamCtrl (
  input  Clock,
  input  Exec,
  input  Fetch,
  input  Load,
  input  Store,
  output MemLoad,
  output MemStore
);

  wire and_1_out;

  and and_1 (and_1_out, Exec, Load);
  and and_2 (MemStore, Exec, Clock, Store);
  or or_1 (MemLoad, Fetch, and_1_out);
endmodule

module Registres (
  input  [2:0] SR1,
  input  [15:0] IN,
  input  [2:0] SR2,
  input  [2:0] DR_SR,
  input  WriteReg,
  input  Clock,
  input  Reset,
  output [15:0] R0,
  output [15:0] OUT_SR1,
  output [15:0] R1,
  output [15:0] R2,
  output [15:0] R3,
  output [15:0] OUT_SR2,
  output [15:0] R4,
  output [15:0] R5,
  output [15:0] OUT_SR,
  output [15:0] R6,
  output [15:0] R7
);

  wire decoder_1_out0, decoder_1_out1, decoder_1_out2, decoder_1_out3, decoder_1_out4, decoder_1_out5,
       decoder_1_out6, decoder_1_out7;

  Decoder #(.select(3), .disabled(0)) decoder_1 (
    .out0(decoder_1_out0), .out1(decoder_1_out1), .out2(decoder_1_out2), .out3(decoder_1_out3),
    .out4(decoder_1_out4), .out5(decoder_1_out5), .out6(decoder_1_out6), .out7(decoder_1_out7), .sel(DR_SR),
    .en(WriteReg));
  Register #(.width(16), .trigger("falling")) u_R0 (.D(IN), .en(decoder_1_out0), .Q(R0), .clk(Clock), .clr(Reset));
  Register #(.width(16), .trigger("falling")) u_R1 (.D(IN), .en(decoder_1_out1), .Q(R1), .clk(Clock), .clr(Reset));
  Register #(.width(16), .trigger("falling")) u_R2 (.D(IN), .en(decoder_1_out2), .Q(R2), .clk(Clock), .clr(Reset));
  Register #(.width(16), .trigger("falling")) u_R3 (.D(IN), .en(decoder_1_out3), .Q(R3), .clk(Clock), .clr(Reset));
  Register #(.width(16), .trigger("falling")) u_R4 (.D(IN), .en(decoder_1_out4), .Q(R4), .clk(Clock), .clr(Reset));
  Register #(.width(16), .trigger("falling")) u_R5 (.D(IN), .en(decoder_1_out5), .Q(R5), .clk(Clock), .clr(Reset));
  Register #(.width(16), .trigger("falling")) u_R6 (.D(IN), .en(decoder_1_out6), .Q(R6), .clk(Clock), .clr(Reset));
  Register #(.width(16), .trigger("falling")) u_R7 (.D(IN), .en(decoder_1_out7), .Q(R7), .clk(Clock), .clr(Reset));
  Multiplexer #(.select(3), .width(16), .enable("false")) multiplexer_1 (
    .in0(R0), .in1(R1), .in2(R2), .in3(R3), .in4(R4), .in5(R5), .in6(R6), .in7(R7), .out(OUT_SR1), .sel(SR1));
  Multiplexer #(.select(3), .width(16), .enable("false")) multiplexer_2 (
    .in0(R0), .in1(R1), .in2(R2), .in3(R3), .in4(R4), .in5(R5), .in6(R6), .in7(R7), .out(OUT_SR2), .sel(SR2));
  Multiplexer #(.select(3), .width(16), .enable("false")) multiplexer_3 (
    .in0(R0), .in1(R1), .in2(R2), .in3(R3), .in4(R4), .in5(R5), .in6(R6), .in7(R7), .out(OUT_SR), .sel(DR_SR));
endmodule

module RegPC (
  input  [8:0] Offset9,
  input  Cond,
  input  Branch,
  input  Clock,
  input  Reset,
  output [15:0] PC
);

  wire and_1_out;
  wire [15:0] adder_1_out, bit_extender_1_out, multiplexer_1_out;

  and and_1 (and_1_out, Cond, Branch);
  assign bit_extender_1_out = {{7{Offset9[8]}}, Offset9};  // Bit_Extender bit_extender_1
  Multiplexer #(.width(16)) multiplexer_1 (
    .in0({16{1'b0}}), .in1(bit_extender_1_out), .out(multiplexer_1_out), .sel(and_1_out));  // open: en
  Adder #(.width(16)) adder_1 (.a(PC), .b(multiplexer_1_out), .out(adder_1_out), .cin(1'b1));  // open: cout
  Register #(.width(16), .trigger("falling")) u_PC (.D(adder_1_out), .Q(PC), .clk(Clock), .clr(Reset));  // open: en
endmodule

module Seq (
  input  ClockOrig,
  input  reset,
  output Fetch,
  output Exec,
  output Clock
);

  Register #(.width(1), .trigger("falling")) register_1 (
    .D(Fetch), .Q(Exec), .clk(ClockOrig), .clr(reset));  // open: en
  not not_1 (Fetch, Exec);
  buf buffer_1 (Clock, ClockOrig);
endmodule
