// Logisim project UE-INF2031L_TPN_rendu_circ_tpnoté2023.circ as structural Verilog
module multiplexer (
  input  in_1,
  input  in_2,
  input  in_3,
  output out_4
);

  wire nand_1_out, nand_2_out, not_1_out;

  not not_1 (not_1_out, in_3);
  nand nand_1 (nand_1_out, in_1, not_1_out);
  nand nand_2 (nand_2_out, in_2, in_3);
  nand nand_3 (out_4, nand_1_out, nand_2_out);
endmodule

module full_adder (
  input  in_1,
  input  in_2,
  input  in_3,
  output out_4,
  output out_5
);

  wire na, nand_1_out, nand_2_out, nand_3_out, nand_4_out, nand_5_out, nand_6_out, nand_7_out, nand_8_out,
       nb, nr;

  not not_1 (na, in_1);
  not not_2 (nb, in_2);
  not not_3 (nr, in_3);
  nand nand_1 (nand_1_out, in_3, in_2, na);
  nand nand_2 (nand_2_out, in_1, nb, in_3);
  nand nand_3 (nand_3_out, in_1, in_2, nr);
  nand nand_4 (nand_4_out, in_2, in_1, in_3);
  nand nand_5 (nand_5_out, nb, na, in_3);
  nand nand_6 (nand_6_out, na, nr, in_2);
  nand nand_7 (nand_7_out, nr, nb, in_1);
  nand nand_8 (nand_8_out, in_1, in_2, in_3);
  nand nand_9 (out_4, nand_1_out, nand_2_out, nand_3_out, nand_4_out);
  nand nand_10 (out_5, nand_5_out, nand_6_out, nand_7_out, nand_8_out);
endmodule

module full_adder2 (
  input  [9:0] in_1,
  input  in_2,
  input  [9:0] in_3,
  output out_4,
  output [9:0] out_5
);

  wire full_adder_1_out_4, full_adder_2_out_4, full_adder_3_out_4, full_adder_4_out_4, full_adder_5_out_4,
       full_adder_6_out_4, full_adder_7_out_4, full_adder_8_out_4, full_adder_9_out_4;

  full_adder full_adder_1 (.in_1(in_3[0]), .in_2(in_1[0]), .in_3(in_2), .out_4(full_adder_1_out_4), .out_5(out_5[0]));
  full_adder full_adder_2 (
    .in_1(in_1[1]), .in_2(in_3[1]), .in_3(full_adder_1_out_4), .out_4(full_adder_2_out_4), .out_5(out_5[1]));
  full_adder full_adder_3 (
    .in_1(in_1[5]), .in_2(in_3[5]), .in_3(full_adder_8_out_4), .out_4(full_adder_3_out_4), .out_5(out_5[5]));
  full_adder full_adder_4 (
    .in_1(in_1[2]), .in_2(in_3[2]), .in_3(full_adder_2_out_4), .out_4(full_adder_4_out_4), .out_5(out_5[2]));
  full_adder full_adder_5 (
    .in_1(in_1[6]), .in_2(in_3[6]), .in_3(full_adder_3_out_4), .out_4(full_adder_5_out_4), .out_5(out_5[6]));
  full_adder full_adder_6 (
    .in_1(in_1[3]), .in_2(in_3[3]), .in_3(full_adder_4_out_4), .out_4(full_adder_6_out_4), .out_5(out_5[3]));
  full_adder full_adder_7 (
    .in_1(in_1[7]), .in_2(in_3[7]), .in_3(full_adder_5_out_4), .out_4(full_adder_7_out_4), .out_5(out_5[7]));
  full_adder full_adder_8 (
    .in_1(in_1[4]), .in_2(in_3[4]), .in_3(full_adder_6_out_4), .out_4(full_adder_8_out_4), .out_5(out_5[4]));
  full_adder full_adder_9 (
    .in_1(in_1[8]), .in_2(in_3[8]), .in_3(full_adder_7_out_4), .out_4(full_adder_9_out_4), .out_5(out_5[8]));
  full_adder full_adder_10 (.in_1(in_1[9]), .in_2(in_3[9]), .in_3(full_adder_9_out_4), .out_4(out_4), .out_5(out_5[9]));

  // Notes on the sheet:
  //   On a 10 PORTES NAND dans un additionneur et on a 10 ADDITIONNEURs
  //   donc on a 100 portes nands
endmodule

module multiplexer_5 (
  input  [4:0] in_1,
  input  [4:0] in_2,
  input  in_3,
  output [4:0] out_4,
  output [4:0] out_5
);

  wire [4:0] nand_1_out, nand_2_out, not_1_out;

  assign not_1_out = ~{5{in_3}};  // NOT_Gate not_1, 5 bits wide
  assign nand_1_out = ~(in_1 & not_1_out);  // NAND_Gate nand_1, 5 bits wide
  assign nand_2_out = ~(in_2 & {5{in_3}});  // NAND_Gate nand_2, 5 bits wide
  assign out_4 = ~(nand_1_out & nand_2_out);  // NAND_Gate nand_3, 5 bits wide

  assign out_5 = {5{in_3}};
endmodule

module exo_final (
  input  [9:0] in_1,
  input  [9:0] in_2,
  input  in_3,
  output out_4
);

  wire full_adder_1_out_4, full_adder_4_out_4, full_adder_6_out_4, full_adder_8_out_4;

  full_adder full_adder_1 (.in_1(in_2[0]), .in_2(in_1[0]), .in_3(in_3), .out_4(full_adder_1_out_4));  // open: out_5
  full_adder full_adder_2 (.in_3(1'b1));  // open: in_1, in_2, out_4, out_5
  full_adder full_adder_3 ();  // open: in_1, in_2, in_3, out_4, out_5
  full_adder full_adder_4 (
    .in_1(in_2[1]), .in_2(in_1[1]), .in_3(full_adder_1_out_4), .out_4(full_adder_4_out_4));  // open: out_5
  full_adder full_adder_5 ();  // open: in_1, in_2, in_3, out_4, out_5
  full_adder full_adder_6 (
    .in_1(in_2[2]), .in_2(in_1[2]), .in_3(full_adder_4_out_4), .out_4(full_adder_6_out_4));  // open: out_5
  full_adder full_adder_7 ();  // open: in_1, in_2, in_3, out_4, out_5
  full_adder full_adder_8 (
    .in_1(in_2[3]), .in_2(in_1[3]), .in_3(full_adder_6_out_4), .out_4(full_adder_8_out_4));  // open: out_5
  full_adder full_adder_9 (.in_1(in_2[4]), .in_2(in_1[4]), .in_3(full_adder_8_out_4), .out_5(out_4));  // open: out_4
  full_adder full_adder_10 ();  // open: in_1, in_2, in_3, out_4, out_5
endmodule
