// Logisim project adder.circ as structural Verilog: 2 circuits, main circuit main
module main (
  input  in_1,
  input  in_2,
  input  in_3,
  output out_4,
  output out_5
);

  wire and_1_out, and_2_out, xor_1_out;

  or or_1 (out_4, and_1_out, and_2_out);
  and and_1 (and_1_out, in_1, in_2);
  and and_2 (and_2_out, xor_1_out, in_3);
  xor xor_1 (xor_1_out, in_1, in_2);
  xor xor_2 (out_5, xor_1_out, in_3);
endmodule

module adder (
  input  in_1,
  input  in_2,
  input  in_3,
  input  in_4,
  input  in_5,
  input  in_6,
  input  in_7,
  input  in_8,
  input  in_9,
  input  in_10,
  output out_11,
  output [7:0] out_12,
  output [3:0] out_13,
  output out_14
);

  wire main_2_out_4, main_3_out_4, main_4_out_4;

  main main_1 (.out_4(out_11), .in_1(in_3), .in_2(in_4), .out_5(out_13[3]), .in_3(main_2_out_4));
  main main_2 (.out_4(main_2_out_4), .in_1(in_1), .in_2(in_2), .out_5(out_13[2]), .in_3(main_3_out_4));
  main main_3 (.out_4(main_3_out_4), .in_1(in_5), .in_2(in_6), .out_5(out_13[1]), .in_3(main_4_out_4));
  main main_4 (.out_4(main_4_out_4), .in_1(in_7), .in_2(in_8), .out_5(out_13[0]), .in_3(in_9));
  Adder adder_1 (.a(8'h80), .b(8'h8c), .out(out_12), .cin(in_10), .cout(out_14));
endmodule
