// Logisim project chaine.circ as structural Verilog: 1 circuit, main circuit main
module main (
  input  reset,
  input  in_2
);

  wire clock_out;
  wire [4:0] counter_1_q;
  wire [6:0] rom_1_data;

  Counter #(.width(5), .max('h1f)) counter_1 (
    .Q(counter_1_q), .clk(clock_out), .clr(reset));  // open: load, D, count, carry
  Clock clock (.out(clock_out));
  ROM #(.addrWidth(5), .dataWidth(7)) rom_1 (.addr(counter_1_q), .data(rom_1_data), .sel(in_2));
  TTY #(.rows(3)) tty_1 (.data(rom_1_data), .clk(clock_out), .we(1'b1), .clr(reset));

  // Notes on the sheet:
  //   contents of rom_1 (hex, n*v repeats v):
  //   74 6f 74 6f 20 66 61 69 74 20 64 75 20 76 65 6c 6f 20 21 21 21
  //   entrée
  //   écran
endmodule
