// Logisim project circuits-sequentiels.circ as structural Verilog: 1 circuit, main circuit main
module main (
  input  [3:0] in_1,
  input  in_2,
  input  in_3,
  input  Reset,
  input  [3:0] in_5,
  output out_6,
  output out_7,
  output [3:0] out_8
);

  wire button_1_out, clock_1_out, clock_2_out, clock_3_out, clock_4_out, d_ff_3_q, d_ff_4_q, d_ff_5_q,
       d_ff_6_q, d_ff_7_q;
  wire [3:0] adder_1_out, register_1_q;

  Clock clock_1 (.out(clock_1_out));
  D_Flip_Flop d_ff_1 (.clk(clock_1_out), .D(out_7), .Q(out_6), .reset(in_3));  // open: Qn, preset, en
  D_Flip_Flop d_ff_2 (.clk(clock_1_out), .D(out_6), .Q(out_7), .preset(in_3));  // open: Qn, en, reset
  Clock clock_2 (.out(clock_2_out));
  D_Flip_Flop d_ff_3 (.clk(clock_2_out), .D(d_ff_7_q), .Q(d_ff_3_q), .preset(Reset));  // open: Qn, en, reset
  D_Flip_Flop d_ff_4 (.clk(clock_2_out), .D(d_ff_3_q), .Q(d_ff_4_q), .reset(Reset));  // open: Qn, preset, en
  D_Flip_Flop d_ff_5 (.clk(clock_2_out), .D(d_ff_4_q), .Q(d_ff_5_q), .reset(Reset));  // open: Qn, preset, en
  D_Flip_Flop d_ff_6 (.clk(clock_2_out), .D(d_ff_5_q), .Q(d_ff_6_q), .reset(Reset));  // open: Qn, preset, en
  D_Flip_Flop d_ff_7 (.clk(clock_2_out), .D(d_ff_6_q), .Q(d_ff_7_q), .reset(Reset));  // open: Qn, preset, en
  LED led_1 (.in(d_ff_3_q));
  LED led_2 (.in(d_ff_4_q));
  LED led_3 (.in(d_ff_5_q));
  LED led_4 (.in(d_ff_6_q));
  LED led_5 (.in(d_ff_7_q));
  Clock clock_3 (.out(clock_3_out));
  Button button_1 (.out(button_1_out));
  D_Flip_Flop d_ff_8 (.clk(clock_3_out), .D(in_1[0]), .Q(out_8[0]), .preset(in_2));  // open: Qn, en, reset
  Clock clock_4 (.out(clock_4_out));
  Hex_Digit_Display hex_digit_display_1 (.value(register_1_q));  // open: dp
  Register #(.width(4)) register_1 (
    .D(adder_1_out), .Q(register_1_q), .clk(clock_4_out), .clr(button_1_out));  // open: en
  D_Flip_Flop d_ff_9 (.clk(clock_3_out), .D(in_1[1]), .Q(out_8[1]), .reset(in_2));  // open: Qn, preset, en
  D_Flip_Flop d_ff_10 (.clk(clock_3_out), .D(in_1[2]), .Q(out_8[2]), .reset(in_2));  // open: Qn, preset, en
  Adder #(.width(4)) adder_1 (.a(register_1_q), .b(in_5), .out(adder_1_out));  // open: cin, cout
  D_Flip_Flop d_ff_11 (.clk(clock_3_out), .D(in_1[3]), .Q(out_8[3]), .reset(in_2));  // open: Qn, preset, en
endmodule
