// Logisim project circuits-sequentiels3.circ as structural Verilog: 1 circuit, main circuit main
module main (
  input  in_1,
  input  in_2,
  output out_3,
  output out_4
);

  wire clock_1_out, d_ff_1_q, d_ff_2_q, d_ff_3_q, not_1_out, or_1_out, or_2_out;
  wire [1:0] and_1_out, register_1_q;

  not not_1 (not_1_out, register_1_q[1]);
  or or_1 (or_1_out, register_1_q[1], register_1_q[0]);
  or or_2 (or_2_out, not_1_out, register_1_q[0]);
  and and_1 (and_1_out[0], in_1, or_1_out);
  and and_2 (and_1_out[1], in_1, or_2_out);
  D_Flip_Flop d_ff_1 (.clk(clock_1_out), .D(in_2), .Q(d_ff_1_q));  // open: Qn, preset, en, reset
  Clock clock_1 (.out(clock_1_out));
  D_Flip_Flop d_ff_2 (.clk(clock_1_out), .D(d_ff_1_q), .Q(d_ff_2_q));  // open: Qn, preset, en, reset
  Register #(.width(2)) register_1 (.D(and_1_out), .Q(register_1_q), .clk(clock_1_out));  // open: en, clr
  D_Flip_Flop d_ff_3 (.clk(clock_1_out), .D(d_ff_2_q), .Q(d_ff_3_q));  // open: Qn, preset, en, reset
  and and_3 (out_3, register_1_q[0], register_1_q[1]);
  and and_4 (out_4, d_ff_1_q, d_ff_2_q, d_ff_3_q);
endmodule
