// Logisim project ct2019.circ as structural Verilog
module impair (
  input  [3:0] in_1,
  output impair
);


  assign impair = in_1[0];
endmodule

module _000_ou_111 (
  input  in_1,
  output out_2
);

  wire and_1_out, and_2_out, and_3_out, and_4_out, and_5_out, and_6_out, clock_1_out, NE, NQ0, NQ1, NQ2,
       or_1_out, or_2_out, Q0, Q1, Q2;

  Clock clock_1 (.out(clock_1_out));
  not not_1 (NE, in_1);
  and and_1 (and_1_out, Q0, NE, NQ1, NQ2);
  and and_2 (and_2_out, NQ0, NE, Q1, NQ2);
  and and_3 (and_3_out, Q0, in_1, NQ1, Q2);
  and and_4 (and_4_out, NQ0, in_1, Q1, Q2);
  D_Flip_Flop d_ff_1 (.clk(clock_1_out), .D(or_2_out), .Q(Q0));  // open: Qn, preset, en, reset
  D_Flip_Flop d_ff_2 (.clk(clock_1_out), .D(or_1_out), .Q(Q1));  // open: Qn, preset, en, reset
  not not_2 (NQ0, Q0);
  or or_1 (or_1_out, and_1_out, and_2_out, and_3_out, and_4_out);
  not not_3 (NQ1, Q1);
  D_Flip_Flop d_ff_3 (.clk(clock_1_out), .D(in_1), .Q(Q2));  // open: Qn, preset, en, reset
  and and_5 (and_5_out, NQ0, NQ2, NQ1, NE);
  and and_6 (and_6_out, NQ0, NQ1, Q2, in_1);
  not not_4 (NQ2, Q2);
  or or_2 (or_2_out, and_5_out, and_6_out);
  and and_7 (out_2, Q1, NQ0);

  // Other names for the same wires on the sheet: E = in_1
endmodule
