// Logisim project ct2020.circ as structural Verilog
module compteur_par_4 (
  input  in_1,
  output [1:0] out_2
);

  wire and_1_out, and_2_out, and_3_out, and_4_out, clock_1_out, not_1_out, not_2_out, not_3_out, or_1_out,
       or_2_out, xor_1_out;

  Clock clock_1 (.out(clock_1_out));
  and and_1 (and_1_out, out_2[0], in_1);
  and and_2 (and_2_out, not_2_out, not_1_out);
  not not_1 (not_1_out, in_1);
  not not_2 (not_2_out, out_2[0]);
  or or_1 (or_1_out, and_1_out, and_2_out);
  D_Flip_Flop d_ff_1 (.clk(clock_1_out), .D(not_2_out), .Q(out_2[0]));  // open: Qn, preset, en, reset
  xor xor_1 (xor_1_out, out_2[0], in_1);
  and and_3 (and_3_out, out_2[1], or_1_out);
  not not_3 (not_3_out, out_2[1]);
  and and_4 (and_4_out, not_3_out, xor_1_out);
  D_Flip_Flop d_ff_2 (.clk(clock_1_out), .D(or_2_out), .Q(out_2[1]));  // open: Qn, preset, en, reset
  or or_2 (or_2_out, and_3_out, and_4_out);
endmodule

module mod16 (
  input  [3:0] in_1,
  output [3:0] out_2
);


  assign out_2 = {in_1[2:0], 1'b0};
endmodule
