// Logisim project ct2022.circ as structural Verilog
module NZP (
  input  [2:0] in_1,
  output out_2,
  output out_3,
  output out_4
);

  wire not_1_out, not_2_out, not_3_out, not_4_out, or_1_out;

  not not_1 (not_1_out, in_1[0]);
  not not_2 (not_2_out, in_1[1]);
  not not_3 (not_3_out, in_1[2]);
  not not_4 (not_4_out, in_1[2]);
  or or_1 (or_1_out, in_1[1], in_1[0]);
  and and_1 (out_3, not_1_out, not_2_out, not_3_out);
  and and_2 (out_4, not_4_out, or_1_out);

  assign out_2 = in_1[2];
endmodule

module decompteur_par_8_par_pas_de_2 (
  output [3:0] out_1
);

  wire and_1_out, and_2_out, and_3_out, clock_1_out, d_ff_1_q, d_ff_2_q, d_ff_3_q, not_4_out, not_5_out,
       not_6_out, or_1_out, xor_1_out;

  not not_1 (out_1[1], d_ff_1_q);
  not not_2 (out_1[3], d_ff_3_q);
  Clock clock_1 (.out(clock_1_out));
  not not_3 (out_1[2], d_ff_2_q);
  not not_4 (not_4_out, d_ff_1_q);
  D_Flip_Flop d_ff_1 (.clk(clock_1_out), .D(not_4_out), .Q(d_ff_1_q));  // open: Qn, preset, en, reset
  xor xor_1 (xor_1_out, d_ff_2_q, d_ff_1_q);
  D_Flip_Flop d_ff_2 (.clk(clock_1_out), .D(xor_1_out), .Q(d_ff_2_q));  // open: Qn, preset, en, reset
  or or_1 (or_1_out, and_1_out, and_2_out, and_3_out);
  D_Flip_Flop d_ff_3 (.clk(clock_1_out), .D(or_1_out), .Q(d_ff_3_q));  // open: Qn, preset, en, reset
  and and_1 (and_1_out, not_5_out, d_ff_1_q, d_ff_2_q);
  and and_2 (and_2_out, d_ff_3_q, d_ff_2_q, not_4_out);
  and and_3 (and_3_out, d_ff_3_q, not_6_out);
  not not_5 (not_5_out, d_ff_3_q);
  not not_6 (not_6_out, d_ff_2_q);

  assign out_1[0] = 1'b1;
endmodule

module \séquence_00_ou_11  (
  input  in_1,
  output out_2
);

  wire and_1_out, and_2_out, and_3_out, and_4_out, and_5_out, and_6_out, and_7_out, clk, not_1_out, Nq0, Nq1,
       Nq2, or_1_out, or_3_out, q0, q1, q2;

  Clock clock_1 (.out(clk));
  not not_1 (not_1_out, in_1);
  D_Flip_Flop d_ff_1 (.clk(clk), .D(not_1_out), .Q(q0));  // open: Qn, preset, en, reset
  and and_1 (and_1_out, q0, q1, Nq2);
  and and_2 (and_2_out, q0, Nq1, Nq2);
  and and_3 (and_3_out, Nq0, Nq1, Nq2, in_1);
  not not_2 (Nq0, q0);
  or or_1 (or_1_out, and_1_out, and_2_out, and_3_out);
  D_Flip_Flop d_ff_2 (.clk(clk), .D(or_1_out), .Q(q1));  // open: Qn, preset, en, reset
  not not_3 (Nq1, q1);
  D_Flip_Flop d_ff_3 (.clk(clk), .D(or_3_out), .Q(q2));  // open: Qn, preset, en, reset
  and and_4 (and_4_out, q1, Nq2, q0);
  not not_4 (Nq2, q2);
  and and_5 (and_5_out, Nq0, Nq1, q2);
  and and_6 (and_6_out, Nq0, q1, Nq2, in_1);
  and and_7 (and_7_out, Nq0, Nq1, q2, in_1);
  or or_2 (out_2, and_4_out, and_5_out);
  or or_3 (or_3_out, and_6_out, and_7_out);
endmodule
