// Logisim project décalage-rotation.circ as structural Verilog
module main (
  input  in_1,
  input  [7:0] in_2,
  input  in_3,
  input  in_4,
  input  [1:0] in_5,
  output out_6,
  output [7:0] out_7
);

  wire nand_1_out, nand_2_out, not_1_out;

  Multiplexer #(.select(2), .width(8)) multiplexer_1 (
    .in0({in_2[6:0], 1'b0}), .in1({1'b0, in_2[7:1]}), .in2({in_2[6:0], in_2[7]}), .in3({in_2[0], in_2[7:1]}),
    .out(out_7), .sel(in_5));  // open: en
  not not_1 (not_1_out, in_4);
  nand nand_1 (nand_1_out, in_1, not_1_out);
  nand nand_2 (nand_2_out, in_3, in_4);
  nand nand_3 (out_6, nand_1_out, nand_2_out);
endmodule

module Exo2 (
  input  [3:0] in_1,
  input  [3:0] in_2,
  input  in_3,
  output [3:0] out_4
);

  wire [3:0] nand_1_out, nand_2_out, not_1_out;

  assign not_1_out = ~{4{in_3}};  // NOT_Gate not_1, 4 bits wide
  assign nand_1_out = ~(in_1 & not_1_out);  // NAND_Gate nand_1, 4 bits wide
  assign nand_2_out = ~(in_2 & {4{in_3}});  // NAND_Gate nand_2, 4 bits wide
  assign out_4 = ~(nand_1_out & nand_2_out);  // NAND_Gate nand_3, 4 bits wide
endmodule
