// Logisim project exercice2.circ as structural Verilog: 1 circuit, main circuit main
module main (
  input  in_1,
  input  in_2,
  input  in_3,
  input  in_4,
  input  in_5,
  input  in_6,
  input  in_7,
  input  in_8,
  input  in_9,
  input  in_10,
  input  in_11,
  input  in_12,
  input  in_13,
  input  in_14,
  input  in_15
);

  wire and_1_out, and_2_out, not_1_out, not_2_out, not_3_out, not_4_out;

  and and_1 (and_1_out, in_5, in_5, in_10);
  and and_2 (and_2_out, in_8, not_1_out);
  not not_1 (not_1_out, in_10);
  or or_1 (in_7, and_1_out, and_2_out);
  not not_2 (not_2_out, in_3);
  not not_3 (not_3_out, in_2);
  not not_4 (not_4_out, in_4);
  and and_3 (in_1, not_2_out, not_3_out, not_4_out);
  and and_4 (in_6, in_4, not_3_out, not_2_out);
  and and_5 (in_9, not_4_out, in_2, not_2_out);
  and and_6 (in_11, in_4, in_2, not_2_out);
  and and_7 (in_12, in_3, not_3_out, not_4_out);
  and and_8 (in_13, in_3, not_3_out, in_4);
  and and_9 (in_14, in_3, in_2, not_4_out);
  and and_10 (in_15, in_3, in_2, in_4);
endmodule
