// Logisim project regfile4.circ as structural Verilog: 2 circuits, main circuit main
module main (
  input  [1:0] in_1,
  input  [1:0] in_2,
  input  [1:0] in_3,
  input  [3:0] in_4,
  input  Write,
  input  Reset,
  output [3:0] out_7,
  output [3:0] out_8
);

  wire clock_1_out;

  Clock clock_1 (.out(clock_1_out));
  regfile4 regfile4_1 (
    .SR1(in_1), .SR2(in_2), .IN(in_4), .DR(in_3), .OUT1(out_7), .OUT2(out_8), .Clock(clock_1_out),
    .Reset(Reset));
endmodule

module regfile4 (
  input  [1:0] SR1,
  input  [1:0] SR2,
  input  [3:0] IN,
  input  [1:0] DR,
  input  Clock,
  input  Reset,
  output [3:0] OUT1,
  output [3:0] OUT2
);

  wire decoder_1_out0, decoder_1_out1, decoder_1_out2, decoder_1_out3, undriven;
  wire [3:0] R0_q, R1_q, R2_q, R3_q;

  Decoder #(.select(2), .disabled(0)) decoder_1 (
    .out0(decoder_1_out0), .out1(decoder_1_out1), .out2(decoder_1_out2), .out3(decoder_1_out3), .sel(DR),
    .en(undriven));
  Register #(.width(4)) R0 (.D(IN), .en(decoder_1_out0), .Q(R0_q), .clk(Clock), .clr(Reset));
  Register #(.width(4)) R1 (.D(IN), .en(decoder_1_out1), .Q(R1_q), .clk(Clock), .clr(Reset));
  Register #(.width(4)) R2 (.D(IN), .en(decoder_1_out2), .Q(R2_q), .clk(Clock), .clr(Reset));
  Register #(.width(4)) R3 (.D(IN), .en(decoder_1_out3), .Q(R3_q), .clk(Clock), .clr(Reset));
  Multiplexer #(.select(2), .width(4), .enable("false")) multiplexer_1 (
    .in0(R0_q), .in1(R1_q), .in2(R2_q), .in3(R3_q), .out(OUT1), .sel(SR1));
  Multiplexer #(.select(2), .width(4), .enable("false")) multiplexer_2 (
    .in0(R0_q), .in1(R1_q), .in2(R2_q), .in3(R3_q), .out(OUT2), .sel(SR2));
endmodule
