// Logisim project tp1.circ as structural Verilog
module decoder (
  input  in_1,
  input  in_2,
  input  in_3,
  output out_4,
  output out_5,
  output out_6,
  output out_7,
  output out_8,
  output out_9,
  output out_10,
  output out_11
);

  wire not_1_out, not_2_out, not_3_out;

  not not_1 (not_1_out, in_1);
  not not_2 (not_2_out, in_2);
  not not_3 (not_3_out, in_3);
  and and_1 (out_4, not_1_out, not_2_out, not_3_out);
  and and_2 (out_5, not_1_out, not_2_out, in_3);
  and and_3 (out_6, not_1_out, in_2, not_3_out);
  and and_4 (out_7, not_1_out, in_2, in_3);
  and and_5 (out_8, in_1, not_2_out, not_3_out);
  and and_6 (out_9, in_1, not_2_out, in_3);
  and and_7 (out_10, in_1, in_2, not_3_out);
  and and_8 (out_11, in_1, in_2, in_3);
endmodule

module multiplexer (
  input  in_1,
  input  in_2,
  input  in_3,
  output out_4
);

  wire and_1_out, and_2_out, not_1_out;

  not not_1 (not_1_out, in_3);
  and and_1 (and_1_out, in_2, in_3);
  and and_2 (and_2_out, in_1, not_1_out);
  or or_1 (out_4, and_1_out, and_2_out);
endmodule

module decoder_lib (
  input  [2:0] in_1,
  output [7:0] out_2
);

  Decoder #(.select(3)) decoder_1 (
    .out0(out_2[0]), .out1(out_2[1]), .out2(out_2[2]), .out3(out_2[3]), .out4(out_2[4]), .out5(out_2[5]),
    .out6(out_2[6]), .out7(out_2[7]), .sel(in_1));  // open: en
endmodule

module multiplexer_lib (
  input  in_1,
  input  in_2,
  input  in_3,
  output out_4
);

  Multiplexer multiplexer_1 (.in0(in_1), .in1(in_2), .out(out_4), .sel(in_3));  // open: en
endmodule
