// Logisim project tp2_aluetu.circ as structural Verilog: 2 circuits, main circuit ALU
module ALU (
  input  [15:0] Input1,
  input  [15:0] Input2,
  input  [15:0] Cst,
  input  e1,
  input  [1:0] e2,
  output [15:0] Output
);

  wire [15:0] adder_1_out, and_1_out, multiplexer_1_out, not_1_out;

  Multiplexer #(.width(16), .enable("false")) multiplexer_1 (
    .in0(Input2), .in1(Cst), .out(multiplexer_1_out), .sel(e1));
  Adder #(.width(16)) adder_1 (.a(multiplexer_1_out), .b(Input1), .out(adder_1_out));  // open: cin, cout
  assign and_1_out = Input1 & multiplexer_1_out;  // AND_Gate and_1, 16 bits wide
  Multiplexer #(.select(2), .width(16), .enable("false")) multiplexer_2 (
    .in0(adder_1_out), .in1(and_1_out), .in2(not_1_out), .out(Output), .sel(e2));  // open: in3
  assign not_1_out = ~Input1;  // NOT_Gate not_1, 16 bits wide
endmodule

module ALU_test (
  input  e1,
  input  [1:0] e2
);

  wire [15:0] alu_1_output;

  ALU alu_1 (.e1(e1), .e2(e2), .Output(alu_1_output), .Input1(16'h1234), .Input2(16'h4567), .Cst({16{1'b1}}));
  // Probe on alu_1_output

  // Notes on the sheet:
  //   Cst
  //   Input1
  //   Input2
endmodule
